// Logisim project project4.circ as structural Verilog: 15 circuits, main circuit main
module main (
  input  [1:0] ROM_Selector,
  input  Clear,
  output [31:0] R15_PC
);

  wire Clock_out, cpu_1_c, cpu_1_n, cpu_1_v, cpu_1_z;
  wire [31:0] cpu_1_r0, cpu_1_r1, cpu_1_r2, cpu_1_r3, cpu_1_r4, cpu_1_r5, cpu_1_r6, cpu_1_r7, cpu_1_r8,
       cpu_1_r9, cpu_1_r10, cpu_1_r11, cpu_1_r12, cpu_1_r13, cpu_1_r14, cpu_1_r15_pc_8;

  // Probe on ROM_Selector
  // Probe on cpu_1_n
  // Probe on cpu_1_z
  // Probe on cpu_1_c
  // Probe on cpu_1_v
  cpu cpu_1 (
    .ROM_Selector(ROM_Selector), .Clear(Clear), .PC(R15_PC), .Clock(Clock_out), .r0(cpu_1_r0), .r5(cpu_1_r5),
    .r10(cpu_1_r10), .r1(cpu_1_r1), .r6(cpu_1_r6), .r11(cpu_1_r11), .r2(cpu_1_r2), .r7(cpu_1_r7),
    .r12(cpu_1_r12), .r3(cpu_1_r3), .r8(cpu_1_r8), .r13(cpu_1_r13), .r4(cpu_1_r4), .r9(cpu_1_r9),
    .r15_PC_8(cpu_1_r15_pc_8), .r14(cpu_1_r14), .N(cpu_1_n), .Z(cpu_1_z), .C(cpu_1_c), .V(cpu_1_v));
  Clock Clock (.out(Clock_out));
  // Probe on R15_PC
  // Probe on cpu_1_r0
  // Probe on cpu_1_r1
  // Probe on cpu_1_r2
  // Probe on cpu_1_r3
  // Probe on cpu_1_r4
  // Probe on cpu_1_r5
  // Probe on cpu_1_r6
  // Probe on cpu_1_r7
  // Probe on cpu_1_r8
  // Probe on cpu_1_r9
  // Probe on cpu_1_r10
  // Probe on cpu_1_r11
  // Probe on cpu_1_r12
  // Probe on cpu_1_r13
  // Probe on cpu_1_r14
  // Probe on cpu_1_r15_pc_8
endmodule

module cpu (
  input  [1:0] ROM_Selector,
  input  Clock,
  input  Clear,
  output N,
  output Z,
  output C,
  output V,
  output [31:0] PC,
  output [31:0] r1,
  output [31:0] r3,
  output [31:0] r5,
  output [31:0] r7,
  output [31:0] r9,
  output [31:0] r11,
  output [31:0] r13,
  output [31:0] r15_PC_8,
  output [31:0] r0,
  output [31:0] r2,
  output [31:0] r4,
  output [31:0] r6,
  output [31:0] r8,
  output [31:0] r10,
  output [31:0] r12,
  output [31:0] r14
);

  wire contol_unit_1_alusrc, contol_unit_1_bl, contol_unit_1_bx_2, contol_unit_1_memtoreg,
       contol_unit_1_memwrite, contol_unit_1_mov, contol_unit_1_pcsrc, contol_unit_1_regwrite;
  wire [1:0] contol_unit_1_alucontrol, contol_unit_1_immsrc, contol_unit_1_regsrc;
  wire [3:0] multiplexer_3_out, multiplexer_4_out;
  wire [31:0] adder_1_out, adder_2_out, alu_1_result, data_mem_1_read_data, Extend_out_3,
       instruction_mem_1_rd, multiplexer_1_out, multiplexer_2_out, multiplexer_5_out, multiplexer_6_out,
       register_file_1_rd1, register_file_1_rd2;

  Multiplexer #(.width(32), .disabled(0), .enable("false")) multiplexer_1 (
    .in0(adder_1_out), .in1(multiplexer_6_out), .out(multiplexer_1_out), .sel(contol_unit_1_pcsrc));
  Register #(.width(32)) register_1 (.D(multiplexer_2_out), .en(1'b1), .Q(PC), .clk(Clock), .clr(Clear));
  Multiplexer #(.width(32), .disabled(0), .enable("false")) multiplexer_2 (
    .in0(multiplexer_1_out), .in1(r14), .out(multiplexer_2_out), .sel(contol_unit_1_bx_2));
  Instruction_Mem instruction_mem_1 (.Function_Switch(ROM_Selector), .A(PC), .RD(instruction_mem_1_rd));
  Adder #(.width(32)) adder_1 (.a(PC), .b(32'h4), .out(adder_1_out));  // open: cin, cout
  contol_unit contol_unit_1 (
    .Cond(instruction_mem_1_rd[31:28]), .ALUFlags({V, C, Z, N}), .Funct(instruction_mem_1_rd[25:20]),
    .PCSrc(contol_unit_1_pcsrc), .RegWrite(contol_unit_1_regwrite), .MemWrite(contol_unit_1_memwrite),
    .MemtoReg(contol_unit_1_memtoreg), .ALUSrc(contol_unit_1_alusrc), .ImmSrc(contol_unit_1_immsrc),
    .RegSrc(contol_unit_1_regsrc), .ALUControl(contol_unit_1_alucontrol), .Op(instruction_mem_1_rd[27:26]),
    .Clock(Clock), .Clear(Clear), .Rd(instruction_mem_1_rd[15:12]), .mov(contol_unit_1_mov),
    .BL(contol_unit_1_bl), .BX(instruction_mem_1_rd[27:4]), .BX_2(contol_unit_1_bx_2));
  Multiplexer #(.width(4), .disabled(0), .enable("false")) multiplexer_3 (
    .in0(instruction_mem_1_rd[19:16]), .in1(4'b1111), .out(multiplexer_3_out), .sel(contol_unit_1_regsrc[0]));
  Multiplexer #(.width(4), .disabled(0), .enable("false")) multiplexer_4 (
    .in0(instruction_mem_1_rd[3:0]), .in1(instruction_mem_1_rd[15:12]), .out(multiplexer_4_out),
    .sel(contol_unit_1_regsrc[1]));
  Adder #(.width(32)) adder_2 (.a(32'h4), .b(adder_1_out), .out(adder_2_out));  // open: cin, cout
  Register_File register_file_1 (
    .A1(multiplexer_3_out), .A2(multiplexer_4_out), .A3(instruction_mem_1_rd[15:12]), .R15_PC(adder_2_out),
    .RD1(register_file_1_rd1), .RD2(register_file_1_rd2), .WE(contol_unit_1_regwrite), .Clock(Clock),
    .WD3(multiplexer_6_out), .Clear(Clear), .LB(contol_unit_1_bl), .R14(r14), .r0(r0), .r1(r1), .r2(r2),
    .r3(r3), .r4(r4), .r5(r5), .r6(r6), .r7(r7), .r8(r8), .r9(r9), .r10(r10), .r11(r11), .r12(r12),
    .r13(r13), .r15_PC_8(r15_PC_8));
  Extend Extend (.in_1(contol_unit_1_immsrc), .in_2(instruction_mem_1_rd[23:0]), .out_3(Extend_out_3));
  ALU alu_1 (
    .B(multiplexer_5_out), .A(register_file_1_rd1), .Result(alu_1_result), .Zero(Z), .Negative(N), .Carry(C),
    .oVerflow(V), .ALU_control(contol_unit_1_alucontrol), .mov(contol_unit_1_mov));
  Multiplexer #(.width(32), .disabled(0), .enable("false")) multiplexer_5 (
    .in0(register_file_1_rd2), .in1(Extend_out_3), .out(multiplexer_5_out), .sel(contol_unit_1_alusrc));
  Data_Mem data_mem_1 (
    .A(alu_1_result[23:0]), .WD(register_file_1_rd2), .Clock(Clock), .WE(contol_unit_1_memwrite),
    .Clear(Clear), .Read_Data(data_mem_1_read_data));
  Multiplexer #(.width(32), .disabled(0), .enable("false")) multiplexer_6 (
    .in0(alu_1_result), .in1(data_mem_1_read_data), .out(multiplexer_6_out), .sel(contol_unit_1_memtoreg));

  // Other names for the same wires on the sheet: R15[31:0] = r15_PC_8

  // Notes on the sheet:
  //   Cond
  //   Op
  //   Funct
  //   Rd
  //   BX
  //   Inst Mem
  //   A1
  //   A2
  //   A3
  //   LB
  //   WD3
  //   PC
endmodule

module contol_unit (
  input  Clear,
  input  Clock,
  input  [3:0] Cond,
  input  [3:0] ALUFlags,
  input  [1:0] Op,
  input  [5:0] Funct,
  input  [3:0] Rd,
  input  [23:0] BX,
  output PCSrc,
  output RegWrite,
  output MemWrite,
  output MemtoReg,
  output ALUSrc,
  output [1:0] ImmSrc,
  output [1:0] RegSrc,
  output [1:0] ALUControl,
  output mov,
  output BL,
  output BX_2
);

  wire decoder_1_memw, decoder_1_nowrite, decoder_1_pcs, decoder_1_regw;
  wire [1:0] decoder_1_flagw;

  Conditional_Logic conditional_logic_1 (
    .PCS(decoder_1_pcs), .RegW(decoder_1_regw), .MemW(decoder_1_memw), .FlagW(decoder_1_flagw), .Cond(Cond),
    .ALU_FLags(ALUFlags), .Clear(Clear), .PCSrc(PCSrc), .RegWrite(RegWrite), .MemWrite(MemWrite),
    .Clock(Clock), .NoWrite(decoder_1_nowrite));
  Decoder decoder_1 (
    .Rd(Rd), .Op(Op), .Funct(Funct), .PCS(decoder_1_pcs), .RegW(decoder_1_regw), .MemW(decoder_1_memw),
    .MemtoReg(MemtoReg), .ALUsrc(ALUSrc), .ImmSrc(ImmSrc), .RegSrc(RegSrc), .ALU_Control(ALUControl),
    .FlagW(decoder_1_flagw), .NoWrite(decoder_1_nowrite), .mov(mov), .BL(BL), .BX_2(BX_2), .Bx(BX));
endmodule

module Conditional_Logic (
  input  Clock,
  input  PCS,
  input  RegW,
  input  NoWrite,
  input  MemW,
  input  [1:0] FlagW,
  input  [3:0] Cond,
  input  [3:0] ALU_FLags,
  input  Clear,
  output PCSrc,
  output RegWrite,
  output MemWrite
);

  wire [0:0] check_condition_1_condex;
  wire [1:0] and_1_out, register_1_q, register_2_q;

  assign and_1_out = FlagW & {1'b0, check_condition_1_condex[0]};  // AND_Gate and_1, 2 bits wide
  Register #(.width(2)) register_1 (.D(ALU_FLags[3:2]), .en(and_1_out[1]), .Q(register_1_q), .clk(Clock), .clr(Clear));
  Register #(.width(2)) register_2 (.D(ALU_FLags[1:0]), .en(and_1_out[0]), .Q(register_2_q), .clk(Clock), .clr(Clear));
  and and_2 (PCSrc, PCS, check_condition_1_condex[0]);
  and and_3 (RegWrite, RegW, ~NoWrite, check_condition_1_condex[0]);  // AND_Gate
  and and_4 (MemWrite, MemW, check_condition_1_condex[0]);
  Check_Condition check_condition_1 (
    .Cond(Cond), .Flags3_2(register_1_q), .Flags1_0(register_2_q), .CondEx(check_condition_1_condex[0]));
endmodule

module Check_Condition (
  input  [1:0] Flags3_2,
  input  [1:0] Flags1_0,
  input  [3:0] Cond,
  output CondEx
);

  wire AL_out, and_1_out, and_2_out, and_3_out, and_4_out, and_5_out, EQ_out, GE_out, GT_out, LT_out,
       xnor_1_out, xnor_2_out, xor_1_out;

  and EQ (EQ_out, ~Cond[0], ~Cond[1], ~Cond[2], ~Cond[3], ~1'b0, ~1'b0, ~1'b0, ~1'b0);  // AND_Gate
  and GE (GE_out, ~Cond[0], Cond[1], ~Cond[2], Cond[3], ~1'b0, 1'b1, ~1'b0, 1'b1);  // AND_Gate
  and LT (LT_out, Cond[0], Cond[1], ~Cond[2], Cond[3], 1'b1, 1'b1, ~1'b0, 1'b1);  // AND_Gate
  and GT (GT_out, ~Cond[0], ~Cond[1], Cond[2], Cond[3], ~1'b0, ~1'b0, 1'b1, 1'b1);  // AND_Gate
  and AL (AL_out, ~Cond[0], Cond[1], Cond[2], Cond[3], ~1'b0, 1'b1, 1'b1, 1'b1);  // AND_Gate
  and and_1 (and_1_out, Flags1_0[1], EQ_out);
  xnor xnor_1 (xnor_1_out, Flags1_0[0], Flags3_2[1]);
  and and_2 (and_2_out, xnor_1_out, GE_out);
  and and_3 (and_3_out, LT_out, xor_1_out);
  xor xor_1 (xor_1_out, Flags1_0[0], Flags3_2[1]);
  and and_4 (and_4_out, ~Flags1_0[1], xnor_2_out);  // AND_Gate
  xnor xnor_2 (xnor_2_out, Flags1_0[0], Flags3_2[1]);
  and and_5 (and_5_out, GT_out, and_4_out);
  or or_1 (CondEx, and_1_out, and_2_out, and_3_out, and_5_out, AL_out);

  // Notes on the sheet:
  //   VCZN
endmodule

module Decoder (
  input  [3:0] Rd,
  input  [1:0] Op,
  input  [5:0] Funct,
  input  [23:0] Bx,
  output PCS,
  output BL,
  output RegW,
  output MemW,
  output MemtoReg,
  output ALUsrc,
  output [1:0] ImmSrc,
  output [1:0] RegSrc,
  output BX_2,
  output mov,
  output [1:0] ALU_Control,
  output [1:0] FlagW,
  output NoWrite
);

  wire main_decoder_1_aluop, main_decoder_1_b;

  PC_Logic pc_logic_1 (.Rd(Rd), .RegW(RegW), .Branch(main_decoder_1_b), .PCS(PCS));
  Main_Decoder main_decoder_1 (
    .B(main_decoder_1_b), .RegW(RegW), .MemW(MemW), .MemtoReg(MemtoReg), .ALUsrc(ALUsrc),
    .ImmSrc0(ImmSrc[0]), .ImmSrc1(ImmSrc[1]), .RegSrc0(RegSrc[0]), .RegSrc1(RegSrc[1]),
    .ALUop(main_decoder_1_aluop), .Op(Op), .Funct(Funct), .mov(mov), .BL(BL), .Bx_2(BX_2), .BX(Bx));
  ALU_Decoder ALU_D (
    .ALUop(main_decoder_1_aluop), .Funct(Funct[4:0]), .Control(ALU_Control), .Flags(FlagW), .No_Write(NoWrite));
endmodule

module PC_Logic (
  input  [3:0] Rd,
  input  RegW,
  input  Branch,
  output PCS
);

  wire and_2_out, and_3_out;
  wire [3:0] and_1_out;

  assign and_1_out = 4'b1111 & Rd;  // AND_Gate and_1, 4 bits wide
  and and_2 (and_2_out, and_1_out[0], and_1_out[1], and_1_out[2], and_1_out[3]);
  and and_3 (and_3_out, and_2_out, RegW);
  or or_1 (PCS, and_3_out, Branch);
endmodule

module Main_Decoder (
  input  [23:0] BX,
  input  [1:0] Op,
  input  [5:0] Funct,
  output Bx_2,
  output BL,
  output B,
  output RegW,
  output MemW,
  output MemtoReg,
  output ALUsrc,
  output ImmSrc0,
  output ImmSrc1,
  output RegSrc0,
  output RegSrc1,
  output ALUop,
  output mov
);

  wire and_1_out, and_2_out, DPi_out, DPreg_out, mov_out, STR_out;

  // Probe on B
  // Probe on MemtoReg
  // Probe on ALUsrc
  // Probe on MemW
  and DPreg (DPreg_out, ~Op[1], ~Op[0], ~Funct[5]);  // AND_Gate
  and DPi (DPi_out, ~Op[1], ~Op[0], Funct[5]);  // AND_Gate
  and STR (STR_out, ~Op[1], Op[0], ~Funct[0]);  // AND_Gate
  and LDR (MemtoReg, ~Op[1], Op[0], Funct[0]);  // AND_Gate
  // Probe on ImmSrc0
  // Probe on ImmSrc1
  or or_1 (RegW, DPreg_out, MemtoReg, DPi_out);
  and and_1 (and_1_out, DPreg_out, DPi_out);
  or or_2 (ALUsrc, DPi_out, MemtoReg, B, STR_out);
  or or_3 (ALUop, DPreg_out, DPi_out);
  and u_mov (mov_out, Funct[4], Funct[3], Funct[1]);
  // Probe on RegW
  and L (BL, Funct[4], B);
  and u_B (B, Op[1], Funct[5], ~Op[0]);  // AND_Gate
  or or_4 (MemW, and_1_out, STR_out);
  or or_5 (ImmSrc0, STR_out, MemtoReg);
  and and_2 (and_2_out, DPi_out, STR_out);
  or or_6 (ImmSrc1, and_2_out, B);
  and and_3 (RegSrc1, ~DPreg_out, STR_out);  // AND_Gate
  and mov_2 (mov, ~BL, mov_out);  // AND_Gate
  // Probe on RegSrc1
  Comparator #(.width(24), .mode("unsigned")) comparator_1 (.a(24'h12fff1), .b(BX), .eq(Bx_2));  // open: gt, lt
  // Probe on B
  // Probe on ALUop

  assign RegSrc0 = B;

  // Other names for the same wires on the sheet: M2R = MemtoReg

  // Notes on the sheet:
  //   1
  //   0
  //   5 4 3 2 1 0
  //   Link Bit
endmodule

module ALU_Decoder (
  input  ALUop,
  input  [4:0] Funct,
  output No_Write,
  output [1:0] Control,
  output [1:0] Flags
);

  wire not_1_out, not_2_out, not_3_out, not_4_out, not_5_out;
  wire [1:0] multiplexer_1_out, multiplexer_2_out;
  wire [3:0] ADD_out;

  not not_1 (not_1_out, Funct[3]);
  not not_2 (not_2_out, Funct[4]);
  not not_3 (not_3_out, Funct[2]);
  not not_4 (not_4_out, Funct[1]);
  not not_5 (not_5_out, Funct[0]);
  and ADD (ADD_out[0], not_4_out, not_3_out, ALUop, Funct[3], not_2_out);
  and SUB (ADD_out[1], not_4_out, Funct[2], ALUop, not_1_out, not_2_out);
  and AND (ADD_out[2], not_4_out, not_3_out, ALUop, not_1_out, not_2_out);
  and ORR (ADD_out[3], not_4_out, not_3_out, ALUop, Funct[3], Funct[4]);
  and CMP (No_Write, ALUop, Funct[0], not_4_out, Funct[2], not_1_out, Funct[4]);
  Multiplexer #(.select(4), .width(2), .disabled(0), .enable("false")) multiplexer_1 (
    .in0(2'b00), .in1(2'b00), .in2(2'b01), .in4(2'b10), .in8(2'b11), .out(multiplexer_1_out), .sel(ADD_out));  // open: in3, in5, in6, in7, in9, in10, in11, in12, in13, in14, in15
  Multiplexer #(.select(2), .width(2), .disabled(0), .enable("false")) multiplexer_2 (
    .in0(2'b11), .in1(2'b11), .in2(2'b10), .in3(2'b10), .out(multiplexer_2_out), .sel(multiplexer_1_out));
  Multiplexer #(.width(2), .disabled(0), .enable("false")) multiplexer_3 (
    .in0(2'b00), .in1(multiplexer_2_out), .out(Flags), .sel(Funct[0]));
  Multiplexer #(.width(2), .disabled(0), .enable("false")) multiplexer_4 (
    .in0(multiplexer_1_out), .in1(2'b01), .out(Control), .sel(No_Write));
endmodule

module Register_File (
  input  [3:0] A1,
  input  [3:0] A2,
  input  [31:0] WD3,
  input  [3:0] A3,
  input  WE,
  input  Clock,
  input  LB,
  input  Clear,
  input  [31:0] R15_PC,
  output [31:0] r0,
  output [31:0] r5,
  output [31:0] r10,
  output [31:0] r1,
  output [31:0] r6,
  output [31:0] r11,
  output [31:0] r2,
  output [31:0] r7,
  output [31:0] r12,
  output [31:0] RD1,
  output [31:0] r3,
  output [31:0] r8,
  output [31:0] r13,
  output [31:0] r4,
  output [31:0] r9,
  output [31:0] r15_PC_8,
  output [31:0] RD2,
  output [31:0] R14
);

  wire and_1_out, and_2_out, and_3_out, and_4_out, and_5_out, and_6_out, and_7_out, and_8_out, and_9_out,
       and_10_out, and_11_out, and_12_out, and_13_out, and_14_out, and_15_out, decoder_1_out0,
       decoder_1_out1, decoder_1_out2, decoder_1_out3, decoder_1_out4, decoder_1_out5, decoder_1_out6,
       decoder_1_out7, decoder_1_out8, decoder_1_out9, decoder_1_out10, decoder_1_out11, decoder_1_out12,
       decoder_1_out13, decoder_1_out14, decoder_1_out15, or_1_out;
  wire [31:0] multiplexer_1_out, subtractor_1_out;

  // Probe on r0
  // Probe on r1
  // Probe on r2
  // Probe on r3
  // Probe on r4
  // Probe on r5
  // Probe on r6
  // Probe on r7
  // Probe on r8
  // Probe on r9
  // Probe on r10
  // Probe on r11
  // Probe on r12
  // Probe on r13
  // Probe on R14
  Decoder_part #(.select(4), .disabled(0), .enable("false")) decoder_1 (
    .out0(decoder_1_out0), .out1(decoder_1_out1), .out2(decoder_1_out2), .out3(decoder_1_out3),
    .out4(decoder_1_out4), .out5(decoder_1_out5), .out6(decoder_1_out6), .out7(decoder_1_out7),
    .out8(decoder_1_out8), .out9(decoder_1_out9), .out10(decoder_1_out10), .out11(decoder_1_out11),
    .out12(decoder_1_out12), .out13(decoder_1_out13), .out14(decoder_1_out14), .out15(decoder_1_out15),
    .sel(A3));
  // Probe on R15_PC
  and and_1 (and_1_out, WE, decoder_1_out14);
  Subtractor #(.width(32)) subtractor_1 (.a(R15_PC), .b(32'h4), .out(subtractor_1_out));  // open: bin, bout
  and and_2 (and_2_out, WE, decoder_1_out0);
  and and_3 (and_3_out, WE, decoder_1_out1);
  and and_4 (and_4_out, WE, decoder_1_out2);
  and and_5 (and_5_out, WE, decoder_1_out3);
  and and_6 (and_6_out, WE, decoder_1_out4);
  and and_7 (and_7_out, WE, decoder_1_out5);
  and and_8 (and_8_out, WE, decoder_1_out6);
  and and_9 (and_9_out, WE, decoder_1_out7);
  and and_10 (and_10_out, WE, decoder_1_out8);
  and and_11 (and_11_out, WE, decoder_1_out9);
  and and_12 (and_12_out, WE, decoder_1_out10);
  and and_13 (and_13_out, WE, decoder_1_out11);
  and and_14 (and_14_out, WE, decoder_1_out12);
  and and_15 (and_15_out, WE, decoder_1_out13);
  or or_1 (or_1_out, and_1_out, LB);
  Multiplexer #(.width(32), .disabled(0), .enable("false")) multiplexer_1 (
    .in0(WD3), .in1(subtractor_1_out), .out(multiplexer_1_out), .sel(LB));
  Register #(.width(32)) register_1 (.D(WD3), .en(and_2_out), .Q(r0), .clk(Clock), .clr(Clear));
  Register #(.width(32)) register_2 (.D(WD3), .en(and_3_out), .Q(r1), .clk(Clock), .clr(Clear));
  Register #(.width(32)) register_3 (.D(WD3), .en(and_4_out), .Q(r2), .clk(Clock), .clr(Clear));
  Register #(.width(32)) register_4 (.D(WD3), .en(and_5_out), .Q(r3), .clk(Clock), .clr(Clear));
  Register #(.width(32)) register_5 (.D(WD3), .en(and_6_out), .Q(r4), .clk(Clock), .clr(Clear));
  Register #(.width(32)) register_6 (.D(WD3), .en(and_7_out), .Q(r5), .clk(Clock), .clr(Clear));
  Register #(.width(32)) register_7 (.D(WD3), .en(and_8_out), .Q(r6), .clk(Clock), .clr(Clear));
  Register #(.width(32)) register_8 (.D(WD3), .en(and_9_out), .Q(r7), .clk(Clock), .clr(Clear));
  Register #(.width(32)) register_9 (.D(WD3), .en(and_10_out), .Q(r8), .clk(Clock), .clr(Clear));
  Register #(.width(32)) register_10 (.D(WD3), .en(and_11_out), .Q(r9), .clk(Clock), .clr(Clear));
  Register #(.width(32)) register_11 (.D(WD3), .en(and_12_out), .Q(r10), .clk(Clock), .clr(Clear));
  Register #(.width(32)) register_12 (.D(WD3), .en(and_13_out), .Q(r11), .clk(Clock), .clr(Clear));
  Register #(.width(32)) register_13 (.D(WD3), .en(and_14_out), .Q(r12), .clk(Clock), .clr(Clear));
  Register #(.width(32)) register_14 (.D(WD3), .en(and_15_out), .Q(r13), .clk(Clock), .clr(Clear));
  Register #(.width(32)) register_15 (.D(multiplexer_1_out), .en(or_1_out), .Q(R14), .clk(Clock), .clr(Clear));
  Multiplexer #(.select(4), .width(32), .disabled(0), .enable("false")) multiplexer_2 (
    .in0(r0), .in1(r1), .in2(r2), .in3(r3), .in4(r4), .in5(r5), .in6(r6), .in7(r7), .in8(r8), .in9(r9),
    .in10(r10), .in11(r11), .in12(r12), .in13(r13), .in14(R14), .in15(R15_PC), .out(RD1), .sel(A1));
  Multiplexer #(.select(4), .width(32), .disabled(0), .enable("false")) multiplexer_3 (
    .in0(r0), .in1(r1), .in2(r2), .in3(r3), .in4(r4), .in5(r5), .in6(r6), .in7(r7), .in8(r8), .in9(r9),
    .in10(r10), .in11(r11), .in12(r12), .in13(r13), .in14(R14), .in15(R15_PC), .out(RD2), .sel(A2));

  assign r15_PC_8 = R15_PC;

  // Other names for the same wires on the sheet: r15[31:0] = R15_PC
endmodule

module Instruction_Mem (
  input  [1:0] Function_Switch,
  input  [31:0] A,
  output [31:0] RD
);

  wire [23:0] divider_1_out;
  wire [31:0] rom_1_data, rom_2_data, rom_3_data, rom_4_data;

  Divider #(.width(24)) divider_1 (.a(A[23:0]), .b(24'h4), .out(divider_1_out));  // open: upper, rem
  ROM #(.addrWidth(24), .dataWidth(32)) rom_1 (.addr(divider_1_out), .data(rom_1_data), .sel(1'b1));
  ROM #(.addrWidth(24), .dataWidth(32)) rom_2 (.addr(divider_1_out), .data(rom_2_data), .sel(1'b1));
  ROM #(.addrWidth(24), .dataWidth(32)) rom_3 (.addr(divider_1_out), .data(rom_3_data), .sel(1'b1));
  ROM #(.addrWidth(24), .dataWidth(32)) rom_4 (.addr(divider_1_out), .data(rom_4_data), .sel(1'b1));
  Multiplexer #(.select(2), .width(32), .disabled(0), .enable("false")) multiplexer_1 (
    .in0(rom_1_data), .in1(rom_2_data), .in2(rom_3_data), .in3(rom_4_data), .out(RD), .sel(Function_Switch));

  // Notes on the sheet:
  //   Sum_array
  //   Fib_iter
  //   fib_rec
  //   find_max
  //   contents of rom_1 (hex, n*v repeats v):
  //   e3a0d0ff e24dd004 e3a00001 e58d0000 e24dd004 e3a00002 e58d0000 e24dd004 e3a00003 e58d0000 e24dd004
  //   e3a00004 e58d0000 e24dd004 e3a00005 e58d0000 e1a0000d e3a01005 eb000000 eafffffe e3a02000 e3a03000
  //   e1520001 a000004 e5904000 e0833004 e2822001 e2800004 eafffff8 e1a00003 e12fff1e
  //   contents of rom_2 (hex, n*v repeats v):
  //   e3a0dc01 e24dd004 e3a00013 e58d0000 eb000000 eafffffe e24dd004 e58d4000 e24dd004 e58d5000 e3a01000
  //   e3a02001 e3a03002 e3500000 a000009 e3500001 a000007 e1530000 ca000004 e0814002 e1a01002 e1a02004
  //   e2833001 eafffff8 e1a00004 e12fff1e
  //   contents of rom_3 (hex, n*v repeats v):
  //   e3a0dc01 e3a00005 eb000000 eafffffe e24dd004 e58d4000 e24dd004 e58d5000 e24dd004 e58d6000 e24dd004
  //   e58de000 e3500001 ca000002 b3a00000 3a00001 ea000008 e1a04000 e2400001 ebffffef e1a05000 e2440002
  //   ebffffec e1a02000 e0850002 eaffffff e59de000 e28dd004 e59d6000 e28dd004 e59d5000 e28dd004 e59d4000
  //   e28dd004 e12fff1e
  //   contents of rom_4 (hex, n*v repeats v):
  //   e3a0dc01 e24dd004 e3a00000 e58d0000 e24dd004 e3a00003 e58d0000 e24dd004 e3a0000e e58d0000 e24dd004
  //   e3e00001 e58d0000 e24dd004 e3a0000a e58d0000 e1a0000d e3a01005 eb000000 eafffffe e3a03000 e3a05000
  //   e1530001 a000005 e5904000 e2800004 e1550004 b1a05004 e2833001 eafffff7 e1a00005 e12fff1e
endmodule

module Extend (
  input  [1:0] in_1,
  input  [23:0] in_2,
  output [31:0] out_3
);

  wire [31:0] bit_extender_1_out, bit_extender_2_out, bit_extender_3_out, shifter_1_out;

  assign bit_extender_1_out = {{24{1'b0}}, in_2[7:0]};  // Bit_Extender bit_extender_1
  assign bit_extender_2_out = {{20{in_2[11]}}, in_2[11:0]};  // Bit_Extender bit_extender_2
  assign bit_extender_3_out = {{8{in_2[23]}}, in_2};  // Bit_Extender bit_extender_3
  // Probe on in_1
  Shifter #(.width(32)) shifter_1 (.in(bit_extender_3_out), .\dist (5'b00010), .out(shifter_1_out));
  Multiplexer #(.select(2), .width(32), .disabled(0), .enable("false")) multiplexer_1 (
    .in0(bit_extender_1_out), .in1(bit_extender_2_out), .in2(shifter_1_out), .out(out_3), .sel(in_1));  // open: in3
endmodule

module Data_Mem (
  input  WE,
  input  [23:0] A,
  input  [31:0] WD,
  input  Clock,
  input  Clear,
  output [31:0] Read_Data
);

  wire not_1_out;

  not not_1 (not_1_out, WE);
  RAM #(.addrWidth(24), .dataWidth(32), .bus("separate")) ram_1 (
    .addr(A), .din(WD), .data(Read_Data), .str(WE), .sel(1'b1), .clk(Clock), .ld(not_1_out), .clr(Clear));
endmodule

module ALU (
  input  [1:0] ALU_control,
  input  [31:0] B,
  input  [31:0] A,
  input  mov,
  output [31:0] Result,
  output Zero,
  output Negative,
  output Carry,
  output oVerflow
);

  wire adder_1_cout, not_2_out, Sum31, xnor_1_out, xor_1_out;
  wire [30:0] adder_1_out;
  wire [31:0] and_1_out, multiplexer_1_out, multiplexer_2_out, not_1_out, or_1_out;

  // Probe on A
  // Probe on B
  Multiplexer #(.width(32), .disabled(0), .enable("false")) multiplexer_1 (
    .in0(A), .in1({32{1'b0}}), .out(multiplexer_1_out), .sel(mov));
  assign not_1_out = ~B;  // NOT_Gate not_1, 32 bits wide
  Multiplexer #(.width(32), .disabled(0), .enable("false")) multiplexer_2 (
    .in0(B), .in1(not_1_out), .out(multiplexer_2_out), .sel(ALU_control[0]));
  not not_2 (not_2_out, ALU_control[1]);
  xor xor_1 (xor_1_out, Sum31, multiplexer_1_out[31]);
  NotExactlyOne xnor_1 (.out(xnor_1_out), .in0(B[31]), .in1(multiplexer_1_out[31]), .in2(ALU_control[0]));
  Adder #(.width(32)) adder_1 (
    .a(multiplexer_2_out), .b(multiplexer_1_out), .out({Sum31, adder_1_out}), .cin(ALU_control[0]),
    .cout(adder_1_cout));
  assign and_1_out = B & multiplexer_1_out;  // AND_Gate and_1, 32 bits wide
  assign or_1_out = B | multiplexer_1_out;  // OR_Gate or_1, 32 bits wide
  Multiplexer #(.select(2), .width(32), .disabled(0), .enable("false")) multiplexer_3 (
    .in0({Sum31, adder_1_out}), .in1({Sum31, adder_1_out}), .in2(and_1_out), .in3(or_1_out),
    .out({Negative, Result[30:0]}), .sel(ALU_control));
  and and_2 (Carry, adder_1_cout, not_2_out);
  and and_3 (oVerflow, not_2_out, xor_1_out, xnor_1_out);
  // Probe on {Negative, Result[30:0]}
  _32_bit_and u_32_bit_and_1 (.in_1({Negative, Result[30:0]}), .out_2(Zero));

  assign Result[31] = Negative;

  // Other names for the same wires on the sheet: Tunnel_to_V_and_C = ALU_control[1]
endmodule

module _32_bit_and (
  input  [31:0] in_1,
  output out_2
);

  and and_1 (out_2, ~in_1[0], ~in_1[1], ~in_1[2], ~in_1[3], ~in_1[4], ~in_1[5], ~in_1[6], ~in_1[7], ~in_1[8], ~in_1[9], ~in_1[10], ~in_1[11], ~in_1[12], ~in_1[13], ~in_1[14], ~in_1[15], ~in_1[16], ~in_1[17], ~in_1[18], ~in_1[19], ~in_1[20], ~in_1[21], ~in_1[22], ~in_1[23], ~in_1[24], ~in_1[25], ~in_1[26], ~in_1[27], ~in_1[28], ~in_1[29], ~in_1[30], ~in_1[31]);  // AND_Gate
endmodule
